# Fritzing sketch PoolAndSpray (saved by Fritzing 0.9.3b)

parts:
  U1 = BNC [package=bnc]
  ORP_Circuit1 = ORP Circuit
  Potentiometer = Rotary Potentiometer (Small) [maximum_resistance=100kΩ package=THT]
  8_Channel_Relay1 = 8 Channel Power Relay
  5V = shrouded pin header, 10 pins [form="♂ (shrouded male)"]
  Composant4 = Arduino Mega ADK (Rev3)
  Squix1 = OLED 0.96" 128x64 I2C SSD1306
  DHT21 = DHT11 Humitidy and Temperature Sensor
  3_3V = shrouded pin header, 10 pins [form="♂ (shrouded male)"]
  DS1_TempSensor = DS18B20 1-Wire Temperature Sensor [part_number=DS18B20]
  2__1______-_+_Out = Camdenboss CTB0158-8 [part_number=CTB0158-8 package=THT]
  R3 = Resistor [tolerance=±5% resistance=4.7k package="0805 [SMD]"]
  OPTOCOUPLEUR_L1521_814_Y = Sharp PC817 [package=THT]
  R4 = Resistor [tolerance=±5% resistance=330 package="0805 [SMD]"]
  R5 = Resistor [tolerance=±5% resistance=4.7k package="0805 [SMD]"]
  +__D__-________+__--__D = Camdenboss CTB0158-8 [part_number=CTB0158-8 package=THT]
  +_OUT_-- = Camdenboss CTB0158-3 [part_number=CTB0158-3 package=THT]
  5V_2 = M16 [package=1x16_machine-pin-header_lock.004]
  GND = M16 [package=1x16_machine-pin-header_lock.004]
  U4 = Header 8 [package=1x08_smd_alt]
  U5 = Header 8 [package=1x08_smd_alt]
  RJ45 = Header 8 [package=1x08_smd_alt]
  RJ45_2 = Header 8 [package=1x08_smd_alt]
  Domino = Header 8 [package=1x08_smd_alt]

nets:
  N1: U1.GND, ORP_Circuit1.GND#5
  N2: U1.OUT, ORP_Circuit1.PRB
  N3: ORP_Circuit1.GND#0, 5V_2.8
  N4: ORP_Circuit1.TX, Composant4.A9
  N5: ORP_Circuit1.RX, GND.13
  VCC: Potentiometer.leg1, 8_Channel_Relay1.VCC, Composant4.5V
  N6: Potentiometer.wiper, Composant4.GND
  N7: Potentiometer.leg2, Composant4.A10
  N8: 8_Channel_Relay1.IN1, Composant4.D22
  N9: 8_Channel_Relay1.IN2, Composant4.D23
  N10: 8_Channel_Relay1.IN3, Composant4.D24
  N11: 8_Channel_Relay1.IN4, Composant4.D25
  N12: 8_Channel_Relay1.IN5, Composant4.D26
  N13: 8_Channel_Relay1.IN6, Composant4.D27
  N14: 8_Channel_Relay1.IN7, Composant4.D28
  N15: 8_Channel_Relay1.IN8, Composant4.D29
  N16: 8_Channel_Relay1.GND, 5V.pin10
  N17: 8_Channel_Relay1.JD-VCC, 5V.pin1
  N18: 8_Channel_Relay1.COM#22, Domino.1
  N19: 8_Channel_Relay1.NO#23, Domino.2
  N20: 8_Channel_Relay1.COM#25, 8_Channel_Relay1.NO#26, 8_Channel_Relay1.NO#29, 8_Channel_Relay1.NO#32, 8_Channel_Relay1.NO#35, U5.1, U5.2, RJ45_2.1
  N21: 8_Channel_Relay1.COM#28, U5.3
  N22: 8_Channel_Relay1.COM#31, U5.4
  N23: 8_Channel_Relay1.COM#34, U5.5
  N24: 5V.pin2, 5V_2.1
  N25: 5V.pin9, GND.1
  N26: Composant4.A8, +__D__-________+__--__D.terminal_8
  N27: Composant4.A11, +__D__-________+__--__D.terminal_2
  N28: Composant4.D21/SCL, Squix1.SCL
  N29: Composant4.D20/SDA, Squix1.SCA
  N30: Composant4.D30, 2__1______-_+_Out.terminal_6
  N31: Composant4.D31, +_OUT_--.terminal_2
  N32: Squix1.VCC, 3_3V.pin6
  N33: Squix1.GND, 3_3V.pin5
  N34: DHT21.VDD, +__D__-________+__--__D.pin6
  N35: DHT21.DATA, +__D__-________+__--__D.pin8
  N36: DHT21.GND, +__D__-________+__--__D.pin7
  N37: DS1_TempSensor.GND, +_OUT_--.pin3, GND.14
  N38: DS1_TempSensor.DQ, R5.Pin_0, +_OUT_--.pin2
  N39: DS1_TempSensor.VDD, R5.Pin_1, +_OUT_--.pin1, 5V_2.12
  N40: 2__1______-_+_Out.pin1, U4.2
  N41: 2__1______-_+_Out.pin2, U4.1
  N42: 2__1______-_+_Out.pin4, GND.2
  N43: 2__1______-_+_Out.terminal_1, R4.Pin_0
  N44: 2__1______-_+_Out.terminal_2, OPTOCOUPLEUR_L1521_814_Y.Pin_1
  N45: 2__1______-_+_Out.terminal_4, R3.Pin_0
  N46: 2__1______-_+_Out.terminal_5, OPTOCOUPLEUR_L1521_814_Y.Pin_4, 5V_2.2
  N47: R3.Pin_1, OPTOCOUPLEUR_L1521_814_Y.Pin_3
  N48: OPTOCOUPLEUR_L1521_814_Y.Pin_2, R4.Pin_1
  N49: +__D__-________+__--__D.pin1, U4.3
  N50: +__D__-________+__--__D.pin2, U4.4
  N51: +__D__-________+__--__D.pin3, U4.5
  N52: +__D__-________+__--__D.terminal_1, 5V_2.5
  N53: +__D__-________+__--__D.terminal_3, GND.11
  N54: +__D__-________+__--__D.terminal_6, 5V_2.15
  N55: +__D__-________+__--__D.terminal_7, GND.15
  N56: U4.8, RJ45.8
  N57: U5.8, RJ45_2.8

notes:
  PH METRE detecteur de niveau liquide
  PH METRE BNC mesure ph
  Canne d'aspiration Liquide
  ALIMENTATION FILTRATION
  + 220v
  pelouse derriere
  potager
  Photinia
  pelouse devant
  +24v
  Pression Filtre
  à sable
  Temp
  EAU

custom parts:
  8 Channel Power Relay: An 8 channel power relay. The module operates at 5V.
  DHT11 Humitidy and Temperature Sensor: DHT11 Humidity and Temperature Sensor
